// Logisim project control_device.circ as structural Verilog: 1 circuit, main circuit main
module main (
);

  wire and_2_out, and_3_out, cdm_16_1_p1, cdm_16_1_p3, cdm_16_1_p4, cdm_16_1_p5, cdm_16_1_p6, cdm_16_1_p7,
       clock, is_active, nor_1_out, not_1_out, not_2_out, pull_resistor_1_node, register_1_q, register_2_q,
       reset_state, \двигать_шашку_out , \лево_верх_out , \лево_низ_out , \право_верх_out , \право_низ_out ,
       \прекратить_ход_out ;
  wire [5:0] d_ff_3_q, register_3_q;
  wire [15:0] address_bus, cdm_16_1_p9, cdm_16_1_p10, data_bus, ram_1_p7, transistor_1_out;
  wire [15:15] pull_resistor_2_node;

  Register #(.width(1)) register_1 (
    .D(is_active), .en(1'b1), .Q(register_1_q), .clk(clock), .clr(pull_resistor_1_node));
  Register #(.width(1), .trigger("low")) register_2 (
    .D(register_1_q), .en(1'b1), .Q(register_2_q), .clk(clock), .clr(pull_resistor_1_node));
  Pull_Resistor pull_resistor_1 (.node(pull_resistor_1_node));
  Button \u_лево_верх  (.out(\лево_верх_out ));
  Button \u_лево_низ  (.out(\лево_низ_out ));
  and and_1 (reset_state, 1'b1, register_2_q);
  // Probe on cdm_16_1_p5
  // Probe on cdm_16_1_p4
  // Probe on cdm_16_1_p3
  // Probe on cdm_16_1_p1
  // CdM_16 cdm_16_1: pin names not known; wires that end beside it: cdm_16_1_p1, clock, cdm_16_1_p3, cdm_16_1_p4, cdm_16_1_p5, cdm_16_1_p6, cdm_16_1_p7, address_bus, cdm_16_1_p9, cdm_16_1_p10
  Button \u_двигать_шашку  (.out(\двигать_шашку_out ));
  D_Flip_Flop d_ff_1 (.clk(\лево_верх_out ), .D(1'b1), .Q(d_ff_3_q[2]), .reset(reset_state));  // open: Qn, preset, en
  D_Flip_Flop d_ff_2 (.clk(\лево_низ_out ), .D(1'b1), .Q(d_ff_3_q[4]), .reset(reset_state));  // open: Qn, preset, en
  Button \u_прекратить_ход  (.out(\прекратить_ход_out ));
  D_Flip_Flop d_ff_3 (
    .clk(\двигать_шашку_out ), .D(1'b1), .Q(d_ff_3_q[0]), .reset(reset_state));  // open: Qn, preset, en
  D_Flip_Flop d_ff_4 (
    .clk(\прекратить_ход_out ), .D(1'b1), .Q(d_ff_3_q[5]), .reset(reset_state));  // open: Qn, preset, en
  not nor_1 (nor_1_out, is_active);  // NOR_Gate
  Transistor #(.\type ("n"), .width(16)) transistor_1 (.in(cdm_16_1_p9), .out(transistor_1_out), .gate(nor_1_out));
  not not_1 (not_1_out, cdm_16_1_p7);
  assign cdm_16_1_p10 = cdm_16_1_p7 ? data_bus : 16'bz;  // Controlled_Buffer controlled_buffer_1
  Button \u_право_верх  (.out(\право_верх_out ));
  D_Flip_Flop d_ff_5 (.clk(\право_верх_out ), .D(1'b1), .Q(d_ff_3_q[1]), .reset(reset_state));  // open: Qn, preset, en
  Button \u_право_низ  (.out(\право_низ_out ));
  D_Flip_Flop d_ff_6 (.clk(\право_низ_out ), .D(1'b1), .Q(d_ff_3_q[3]), .reset(reset_state));  // open: Qn, preset, en
  assign data_bus = not_1_out ? transistor_1_out : 16'bz;  // Controlled_Buffer controlled_buffer_2
  Clock clock_1 (.out(clock));
  and and_2 (and_2_out, cdm_16_1_p7, ~is_active);  // AND_Gate
  assign data_bus = and_2_out ? ram_1_p7 : 16'bz;  // Controlled_Buffer controlled_buffer_3
  // RAM ram_1: pin names not known; wires that end beside it: address_bus, address_bus, 1'b1, cdm_16_1_p6, clock, cdm_16_1_p7, ram_1_p7
  assign ram_1_p7 = and_3_out ? data_bus : 16'bz;  // Controlled_Buffer controlled_buffer_4
  and and_3 (and_3_out, ~cdm_16_1_p7, ~is_active);  // AND_Gate
  // Probe on register_3_q
  Register #(.width(6)) register_3 (
    .D(d_ff_3_q), .en(1'b1), .Q(register_3_q), .clk(clock), .clr(pull_resistor_2_node[15]));
  Pull_Resistor pull_resistor_2 (.node(pull_resistor_2_node[15]));
  not not_2 (not_2_out, address_bus[0]);
  and and_4 (is_active, not_2_out, address_bus[1], address_bus[2], address_bus[3], address_bus[4], address_bus[5], address_bus[6], address_bus[7], address_bus[9], address_bus[10], address_bus[11], address_bus[12], address_bus[13], address_bus[14], address_bus[15], address_bus[8]);
  assign data_bus = is_active ? {{10{pull_resistor_2_node[15]}}, register_3_q} : 16'bz;  // Controlled_Buffer controlled_buffer_5

  // Notes on the sheet:
  //   блокировка процессора
  //   блокировка памяти
endmodule
