// Logisim project control_device_backup.circ as structural Verilog: 1 circuit, main circuit main
module main (
);

  wire and_1_out, and_2_out, and_3_out, and_4_out, cdm_16_1_p1, cdm_16_1_p2, cdm_16_1_p3, cdm_16_1_p4,
       cdm_16_1_p5, cdm_16_1_p6, cdm_16_1_p7, nor_1_out, not_1_out, not_2_out, pull_resistor_1_node,
       register_1_q, register_2_q, \двигать_шашку_out , \лево_верх_out , \лево_низ_out , \право_верх_out ,
       \право_низ_out , \прекратить_ход_out ;
  wire [5:0] d_ff_3_q;
  wire [15:0] cdm_16_1_p8, cdm_16_1_p9, cdm_16_1_p10, controlled_buffer_2_out, ram_1_p6, register_3_q,
       transistor_1_out;

  Register #(.width(1)) register_1 (
    .D(and_4_out), .en(1'b1), .Q(register_1_q), .clk(cdm_16_1_p2), .clr(pull_resistor_1_node));
  Register #(.width(1), .trigger("low")) register_2 (
    .D(register_1_q), .en(1'b1), .Q(register_2_q), .clk(cdm_16_1_p2), .clr(pull_resistor_1_node));
  Pull_Resistor pull_resistor_1 (.node(pull_resistor_1_node));
  Button \u_лево_верх  (.out(\лево_верх_out ));
  Button \u_лево_низ  (.out(\лево_низ_out ));
  and and_1 (and_1_out, 1'b1, register_2_q);
  // Probe on cdm_16_1_p5
  // Probe on cdm_16_1_p4
  // Probe on cdm_16_1_p3
  // Probe on cdm_16_1_p1
  // CdM_16 cdm_16_1: pin names not known; wires that end beside it: cdm_16_1_p1, cdm_16_1_p2, cdm_16_1_p3, cdm_16_1_p4, cdm_16_1_p5, cdm_16_1_p6, cdm_16_1_p7, cdm_16_1_p8, cdm_16_1_p9, cdm_16_1_p10
  Button \u_двигать_шашку  (.out(\двигать_шашку_out ));
  D_Flip_Flop d_ff_1 (.clk(\лево_верх_out ), .D(1'b1), .Q(d_ff_3_q[2]), .reset(and_1_out));  // open: Qn, preset, en
  D_Flip_Flop d_ff_2 (.clk(\лево_низ_out ), .D(1'b1), .Q(d_ff_3_q[4]), .reset(and_1_out));  // open: Qn, preset, en
  Button \u_прекратить_ход  (.out(\прекратить_ход_out ));
  D_Flip_Flop d_ff_3 (.clk(\двигать_шашку_out ), .D(1'b1), .Q(d_ff_3_q[0]), .reset(and_1_out));  // open: Qn, preset, en
  D_Flip_Flop d_ff_4 (
    .clk(\прекратить_ход_out ), .D(1'b1), .Q(d_ff_3_q[5]), .reset(and_1_out));  // open: Qn, preset, en
  Clock clock_1 (.out(cdm_16_1_p2));
  not nor_1 (nor_1_out, and_4_out);  // NOR_Gate
  Transistor #(.\type ("n"), .width(16)) transistor_1 (.in(cdm_16_1_p9), .out(transistor_1_out), .gate(nor_1_out));
  not not_1 (not_1_out, cdm_16_1_p7);
  assign cdm_16_1_p10 = cdm_16_1_p7 ? controlled_buffer_2_out : 16'bz;  // Controlled_Buffer controlled_buffer_1
  Button \u_право_верх  (.out(\право_верх_out ));
  D_Flip_Flop d_ff_5 (.clk(\право_верх_out ), .D(1'b1), .Q(d_ff_3_q[1]), .reset(and_1_out));  // open: Qn, preset, en
  Button \u_право_низ  (.out(\право_низ_out ));
  D_Flip_Flop d_ff_6 (.clk(\право_низ_out ), .D(1'b1), .Q(d_ff_3_q[3]), .reset(and_1_out));  // open: Qn, preset, en
  assign controlled_buffer_2_out = not_1_out ? transistor_1_out : 16'bz;  // Controlled_Buffer controlled_buffer_2
  and and_2 (and_2_out, cdm_16_1_p7, ~and_4_out);  // AND_Gate
  assign controlled_buffer_2_out = and_2_out ? ram_1_p6 : 16'bz;  // Controlled_Buffer controlled_buffer_3
  // RAM ram_1: pin names not known; wires that end beside it: cdm_16_1_p8, 1'b1, cdm_16_1_p6, cdm_16_1_p2, cdm_16_1_p7, ram_1_p6
  assign ram_1_p6 = and_3_out ? controlled_buffer_2_out : 16'bz;  // Controlled_Buffer controlled_buffer_4
  and and_3 (and_3_out, ~cdm_16_1_p7, ~and_4_out);  // AND_Gate
  assign controlled_buffer_2_out = and_4_out ? {{10{register_3_q[15]}}, register_3_q[5:0]} : 16'bz;  // Controlled_Buffer controlled_buffer_5
  // Probe on register_3_q[5:0]
  Register #(.width(6)) register_3 (
    .D(d_ff_3_q), .en(1'b1), .Q(register_3_q[5:0]), .clk(cdm_16_1_p2), .clr(register_3_q[15]));
  Pull_Resistor pull_resistor_2 (.node(register_3_q[15]));
  not not_2 (not_2_out, cdm_16_1_p8[0]);
  and and_4 (and_4_out, not_2_out, cdm_16_1_p8[1], cdm_16_1_p8[2], cdm_16_1_p8[3], cdm_16_1_p8[4], cdm_16_1_p8[5], cdm_16_1_p8[6], cdm_16_1_p8[7], cdm_16_1_p8[9], cdm_16_1_p8[10], cdm_16_1_p8[11], cdm_16_1_p8[12], cdm_16_1_p8[13], cdm_16_1_p8[14], cdm_16_1_p8[15], cdm_16_1_p8[8]);

  // Notes on the sheet:
  //   блокировка процессора
  //   блокировка памяти
endmodule
